// Logisim project Lab02.circ as structural Verilog: 3 circuits, main circuit main
module main (
  input  A2,
  input  B2,
  input  C2,
  input  D2,
  input  A1,
  input  B1,
  input  C1,
  output True2,
  output True1
);

  Equation_2 equation_2_1 (.In1A(A2), .In1B(B2), .In1C(C2), .In1D(D2), .out_5(True2));
  Equation_1 equation_1_1 (.In1A(A1), .In1B(B1), .In1C(C1), .out_4(True1));

  // Notes on the sheet:
  //   Nursultan_Yerlanuly_02_2 March
endmodule

module Equation_2 (
  input  In1A,
  input  In1B,
  input  In1C,
  input  In1D,
  output out_5
);

  wire and_1_out, and_2_out, and_3_out, and_4_out;

  and and_1 (and_1_out, ~In1A, ~In1B, In1C, ~In1D);  // AND_Gate
  and and_2 (and_2_out, ~In1A, In1B, In1C, In1D);  // AND_Gate
  and and_3 (and_3_out, ~In1A, In1B, In1C, ~In1D);  // AND_Gate
  and and_4 (and_4_out, In1A, In1B, In1C, ~In1D);  // AND_Gate
  or or_1 (out_5, and_1_out, and_2_out, and_3_out, and_4_out);

  // Notes on the sheet:
  //   (!A!BC!D) + (!ABCD) + (!ABC!D) + (ABC!D)
endmodule

module Equation_1 (
  input  In1A,
  input  In1B,
  input  In1C,
  output out_4
);

  wire and_1_out, and_2_out, and_3_out;

  and and_1 (and_1_out, ~In1A, In1B, ~In1C);  // AND_Gate
  and and_2 (and_2_out, In1A, ~In1B, ~In1C);  // AND_Gate
  and and_3 (and_3_out, In1A, In1B, In1C);
  or or_1 (out_4, and_1_out, and_2_out, and_3_out);

  // Notes on the sheet:
  //   (!AB!C) + (A!B!C) + (ABC)
endmodule
