// Logisim project main.circ as structural Verilog: 7 circuits, main circuit main
module main (
  input  Reset,
  input  [2:0] in_2
);

  wire clk_out;
  wire [3:0] universal_1_kek;

  Clock #(.highDuration(4), .lowDuration(4)) clk (.out(clk_out));
  Clock sysclk ();  // open: out
  // Probe on universal_1_kek
  Universal universal_1 (.clk(clk_out), .reset(Reset), .Selector(in_2), .kek(universal_1_kek));
  Hex_Digit_Display hex_digit_display_1 (.value(universal_1_kek));  // open: dp
endmodule

module Asyncnhronousupcounter (
  input  clk,
  input  rst,
  output [3:0] Up
);

  wire d_ff_1_qn, d_ff_2_qn, d_ff_3_qn, d_ff_4_qn;

  D_Flip_Flop d_ff_1 (.D(d_ff_1_qn), .clk(clk), .Q(Up[0]), .Qn(d_ff_1_qn), .reset(rst));  // open: preset
  D_Flip_Flop d_ff_2 (.D(d_ff_2_qn), .clk(d_ff_1_qn), .Q(Up[1]), .Qn(d_ff_2_qn), .reset(rst));  // open: preset
  D_Flip_Flop d_ff_3 (.D(d_ff_3_qn), .clk(d_ff_2_qn), .Q(Up[2]), .Qn(d_ff_3_qn), .reset(rst));  // open: preset
  D_Flip_Flop d_ff_4 (.D(d_ff_4_qn), .clk(d_ff_3_qn), .Q(Up[3]), .Qn(d_ff_4_qn), .reset(rst));  // open: preset
endmodule

module asynchronousdowncounter (
  input  clk,
  input  rst,
  output [3:0] Down
);

  wire d_ff_1_qn, d_ff_2_qn, d_ff_3_qn, d_ff_4_qn;

  D_Flip_Flop d_ff_1 (.D(d_ff_1_qn), .clk(clk), .Q(Down[0]), .Qn(d_ff_1_qn), .preset(rst), .reset(rst));
  D_Flip_Flop d_ff_2 (.D(d_ff_2_qn), .clk(Down[0]), .Q(Down[1]), .Qn(d_ff_2_qn), .preset(rst), .reset(rst));
  D_Flip_Flop d_ff_3 (.D(d_ff_3_qn), .clk(Down[1]), .Q(Down[2]), .Qn(d_ff_3_qn), .preset(rst), .reset(rst));
  D_Flip_Flop d_ff_4 (.D(d_ff_4_qn), .clk(Down[2]), .Q(Down[3]), .Qn(d_ff_4_qn), .preset(rst), .reset(rst));
endmodule

module Asynchronousdecadecounter (
  input  clk,
  input  rstt,
  output [3:0] out_3
);

  wire and_1_out, d_ff_1_qn, d_ff_2_qn, d_ff_3_qn, d_ff_4_qn, or_1_out;

  D_Flip_Flop d_ff_1 (.D(d_ff_1_qn), .clk(clk), .Q(out_3[0]), .Qn(d_ff_1_qn), .reset(or_1_out));  // open: preset
  or or_1 (or_1_out, rstt, and_1_out);
  D_Flip_Flop d_ff_2 (.D(d_ff_2_qn), .clk(d_ff_1_qn), .Q(out_3[1]), .Qn(d_ff_2_qn), .reset(or_1_out));  // open: preset
  D_Flip_Flop d_ff_3 (.D(d_ff_3_qn), .clk(d_ff_2_qn), .Q(out_3[2]), .Qn(d_ff_3_qn), .reset(or_1_out));  // open: preset
  D_Flip_Flop d_ff_4 (.D(d_ff_4_qn), .clk(d_ff_3_qn), .Q(out_3[3]), .Qn(d_ff_4_qn), .reset(or_1_out));  // open: preset
  and and_1 (and_1_out, out_3[3], out_3[1]);
endmodule

module Synchronousringcounter (
  input  clk,
  input  reset,
  output [3:0] out_3
);

  D_Flip_Flop d_ff_1 (.D(out_3[3]), .clk(clk), .Q(out_3[0]), .preset(reset));  // open: Qn, reset
  D_Flip_Flop d_ff_2 (.D(out_3[0]), .clk(clk), .Q(out_3[1]), .reset(reset));  // open: Qn, preset
  D_Flip_Flop d_ff_3 (.D(out_3[1]), .clk(clk), .Q(out_3[2]), .reset(reset));  // open: Qn, preset
  D_Flip_Flop d_ff_4 (.D(out_3[2]), .clk(clk), .Q(out_3[3]), .reset(reset));  // open: Qn, preset
endmodule

module Synhronouscounter (
  input  clk,
  input  reset,
  output [3:0] out_3
);

  wire d_ff_4_qn;

  D_Flip_Flop d_ff_1 (.D(d_ff_4_qn), .clk(clk), .Q(out_3[0]), .preset(reset));  // open: Qn, reset
  D_Flip_Flop d_ff_2 (.D(out_3[0]), .clk(clk), .Q(out_3[1]));  // open: Qn, preset, reset
  D_Flip_Flop d_ff_3 (.D(out_3[1]), .clk(clk), .Q(out_3[2]));  // open: Qn, preset, reset
  D_Flip_Flop d_ff_4 (.D(out_3[2]), .clk(clk), .Q(out_3[3]), .Qn(d_ff_4_qn), .reset(reset));  // open: preset
endmodule

module Universal (
  input  clk,
  input  reset,
  input  [2:0] Selector,
  output [3:0] kek
);

  wire [3:0] asynchronousdecadecounter_1_out_3, asynchronousdowncounter_1_down, asyncnhronousupcounter_1_up,
       synchronousringcounter_1_out_3, synhronouscounter_1_out_3;

  Asyncnhronousupcounter asyncnhronousupcounter_1 (.clk(clk), .rst(reset), .Up(asyncnhronousupcounter_1_up));
  asynchronousdowncounter asynchronousdowncounter_1 (.clk(clk), .rst(reset), .Down(asynchronousdowncounter_1_down));
  Asynchronousdecadecounter asynchronousdecadecounter_1 (
    .clk(clk), .rstt(reset), .out_3(asynchronousdecadecounter_1_out_3));
  Synchronousringcounter synchronousringcounter_1 (.clk(clk), .reset(reset), .out_3(synchronousringcounter_1_out_3));
  Synhronouscounter synhronouscounter_1 (.clk(clk), .reset(reset), .out_3(synhronouscounter_1_out_3));
  Multiplexer #(.select(3), .width(4)) multiplexer_1 (
    .in0(asyncnhronousupcounter_1_up), .in1(asynchronousdowncounter_1_down),
    .in3(asynchronousdecadecounter_1_out_3), .in5(synchronousringcounter_1_out_3),
    .in7(synhronouscounter_1_out_3), .out(kek), .sel(Selector));  // open: in2, in4, in6
endmodule
