// Logisim project Onebit.circ as structural Verilog: 2 circuits, main circuit main
module main (
  input  in_1,
  input  in_2,
  output CarryOUT,
  output SUM
);

  Onebitadder onebitadder_1 (.In1(in_1), .In2(in_2), .Cout(CarryOUT), .Sum(SUM));
endmodule

module Onebitadder (
  input  In1,
  input  In2,
  output Cout,
  output Sum
);

  wire and_2_out, and_3_out, not_1_out, not_2_out;

  not not_1 (not_1_out, In1);
  not not_2 (not_2_out, In2);
  and and_1 (Cout, In1, In2);
  and and_2 (and_2_out, not_1_out, In2);
  and and_3 (and_3_out, In1, not_2_out);
  or or_1 (Sum, and_2_out, and_3_out);
endmodule
